// Logisim project contador.circ as structural Verilog: 1 circuit, main circuit main
module main (
  output out_1,
  output out_2,
  output out_3,
  output out_4
);

  wire and_1_out, and_2_out, clock_1_out;

  T_Flip_Flop t_ff_1 (.clk(clock_1_out), .T(and_1_out), .Q(out_1));  // open: Qn, preset, reset, en
  and and_1 (and_1_out, out_2, out_3, out_4);
  T_Flip_Flop t_ff_2 (.clk(clock_1_out), .T(and_2_out), .Q(out_2));  // open: Qn, preset, reset, en
  and and_2 (and_2_out, out_3, out_4);
  T_Flip_Flop t_ff_3 (.clk(clock_1_out), .T(out_4), .Q(out_3));  // open: Qn, preset, reset, en
  T_Flip_Flop t_ff_4 (.clk(clock_1_out), .T(clock_1_out), .Q(out_4));  // open: Qn, preset, reset, en
  Clock clock_1 (.out(clock_1_out));

  // Notes on the sheet:
  //   T3
  //   T2
  //   T1
  //   T0
endmodule
