// Logisim project ucontrol.circ as structural Verilog: 13 circuits, main circuit x0
module x0 (
  input  [3:0] q,
  input  [3:0] t,
  output out_3
);

  wire and_1_out, and_2_out, decoder_1_out1, decoder_1_out2, decoder_1_out3, decoder_1_out4, decoder_2_out0,
       decoder_2_out3, decoder_2_out6, or_1_out;

  Decoder #(.select(4)) decoder_1 (
    .out1(decoder_1_out1), .out2(decoder_1_out2), .out3(decoder_1_out3), .out4(decoder_1_out4), .sel(q));  // open: out0, out5, out6, out7, out8, out9, out10, out11, out12, out13, out14, out15, en
  Decoder #(.select(4)) decoder_2 (
    .out0(decoder_2_out0), .out3(decoder_2_out3), .out6(decoder_2_out6), .sel(t));  // open: out1, out2, out4, out5, out7, out8, out9, out10, out11, out12, out13, out14, out15, en
  or or_1 (or_1_out, decoder_1_out1, decoder_1_out2, decoder_1_out3, decoder_1_out4);
  and and_1 (and_1_out, or_1_out, decoder_2_out3);
  and and_2 (and_2_out, decoder_1_out4, decoder_2_out6);
  or X0 (out_3, and_1_out, and_2_out, decoder_2_out0);
endmodule

module x2 (
  input  [3:0] q,
  input  [3:0] t,
  output out_3
);

  wire and_1_out, decoder_1_out1, decoder_1_out2, decoder_1_out3, decoder_1_out4, decoder_2_out1,
       decoder_2_out4, decoder_2_out6, or_1_out, q0t6_out, q3t4_out;

  Decoder #(.select(4)) decoder_1 (
    .out1(decoder_1_out1), .out2(decoder_1_out2), .out3(decoder_1_out3), .out4(decoder_1_out4), .sel(q));  // open: out0, out5, out6, out7, out8, out9, out10, out11, out12, out13, out14, out15, en
  Decoder #(.select(4)) decoder_2 (
    .out1(decoder_2_out1), .out4(decoder_2_out4), .out6(decoder_2_out6), .sel(t));  // open: out0, out2, out3, out5, out7, out8, out9, out10, out11, out12, out13, out14, out15, en
  or or_1 (or_1_out, decoder_1_out1, decoder_1_out2, decoder_1_out3, decoder_1_out4);
  and q3t4 (q3t4_out, decoder_1_out4, decoder_2_out4);
  and q0t6 (q0t6_out, decoder_1_out1, decoder_2_out6);
  and and_1 (and_1_out, or_1_out, decoder_2_out4);
  or or_2 (out_3, and_1_out, q3t4_out, q0t6_out, decoder_2_out1);
endmodule

module x3 (
  input  [3:0] q,
  input  [3:0] t,
  output out_3
);

  wire and_1_out, decoder_1_out1, decoder_1_out2, decoder_1_out3, decoder_1_out4, decoder_2_out1,
       decoder_2_out4, decoder_2_out7, or_1_out, q3t7_out;

  Decoder #(.select(4)) decoder_1 (
    .out1(decoder_1_out1), .out2(decoder_1_out2), .out3(decoder_1_out3), .out4(decoder_1_out4), .sel(q));  // open: out0, out5, out6, out7, out8, out9, out10, out11, out12, out13, out14, out15, en
  Decoder #(.select(4)) decoder_2 (
    .out1(decoder_2_out1), .out4(decoder_2_out4), .out7(decoder_2_out7), .sel(t));  // open: out0, out2, out3, out5, out6, out8, out9, out10, out11, out12, out13, out14, out15, en
  or or_1 (or_1_out, decoder_1_out1, decoder_1_out2, decoder_1_out3, decoder_1_out4);
  and and_1 (and_1_out, or_1_out, decoder_2_out4);
  and q3t7 (q3t7_out, decoder_1_out4, decoder_2_out7);
  or or_2 (out_3, and_1_out, decoder_2_out1, q3t7_out);
endmodule

module x1 (
  input  [3:0] q,
  input  [3:0] t,
  output out_3
);

  wire decoder_1_out1, decoder_1_out2, decoder_2_out5, q0_q1_out;

  Decoder #(.select(4)) decoder_1 (
    .out1(decoder_1_out1), .out2(decoder_1_out2), .sel(q));  // open: out0, out3, out4, out5, out6, out7, out8, out9, out10, out11, out12, out13, out14, out15, en
  Decoder #(.select(4)) decoder_2 (
    .out5(decoder_2_out5), .sel(t));  // open: out0, out1, out2, out3, out4, out6, out7, out8, out9, out10, out11, out12, out13, out14, out15, en
  or q0_q1 (q0_q1_out, decoder_1_out1, decoder_1_out2);
  and and_1 (out_3, q0_q1_out, decoder_2_out5);
endmodule

module x5 (
  input  [3:0] q,
  input  [3:0] t,
  output out_3
);

  wire decoder_1_out1, decoder_2_out7;

  Decoder #(.select(4)) decoder_1 (
    .out1(decoder_1_out1), .sel(q));  // open: out0, out2, out3, out4, out5, out6, out7, out8, out9, out10, out11, out12, out13, out14, out15, en
  Decoder #(.select(4)) decoder_2 (
    .out7(decoder_2_out7), .sel(t));  // open: out0, out1, out2, out3, out4, out5, out6, out8, out9, out10, out11, out12, out13, out14, out15, en
  and q0t7 (out_3, decoder_1_out1, decoder_2_out7);
endmodule

module x8 (
  input  [3:0] q,
  input  [3:0] t,
  output out_3
);

  wire and_1_out, decoder_1_out5, decoder_1_out7, decoder_1_out8, decoder_2_out1, decoder_2_out2,
       decoder_2_out3, decoder_2_out4, or_1_out, q2t5_out, q3t8_out;

  Decoder #(.select(4)) decoder_1 (
    .out5(decoder_1_out5), .out7(decoder_1_out7), .out8(decoder_1_out8), .sel(t));  // open: out0, out1, out2, out3, out4, out6, out9, out10, out11, out12, out13, out14, out15, en
  Decoder #(.select(4)) decoder_2 (
    .out1(decoder_2_out1), .out2(decoder_2_out2), .out3(decoder_2_out3), .out4(decoder_2_out4), .sel(q));  // open: out0, out5, out6, out7, out8, out9, out10, out11, out12, out13, out14, out15, en
  or or_1 (or_1_out, decoder_2_out1, decoder_2_out2);
  and and_1 (and_1_out, or_1_out, decoder_1_out7);
  and q2t5 (q2t5_out, decoder_2_out3, decoder_1_out5);
  and q3t8 (q3t8_out, decoder_2_out4, decoder_1_out8);
  or or_2 (out_3, and_1_out, q2t5_out, q3t8_out);
endmodule

module x7 (
  input  [3:0] q,
  input  [3:0] t,
  output out_3
);

  wire decoder_1_out2, decoder_2_out6;

  Decoder #(.select(4)) decoder_1 (
    .out2(decoder_1_out2), .sel(q));  // open: out0, out1, out3, out4, out5, out6, out7, out8, out9, out10, out11, out12, out13, out14, out15, en
  Decoder #(.select(4)) decoder_2 (
    .out6(decoder_2_out6), .sel(t));  // open: out0, out1, out2, out3, out4, out5, out7, out8, out9, out10, out11, out12, out13, out14, out15, en
  and q1t6 (out_3, decoder_1_out2, decoder_2_out6);
endmodule

module x9 (
  input  [3:0] in_1,
  input  [3:0] in_2,
  output out_3
);

  wire decoder_1_out2, decoder_2_out7;

  Decoder #(.select(4)) decoder_1 (
    .out2(decoder_1_out2), .sel(in_1));  // open: out0, out1, out3, out4, out5, out6, out7, out8, out9, out10, out11, out12, out13, out14, out15, en
  Decoder #(.select(4)) decoder_2 (
    .out7(decoder_2_out7), .sel(in_2));  // open: out0, out1, out2, out3, out4, out5, out6, out8, out9, out10, out11, out12, out13, out14, out15, en
  and q1t7 (out_3, decoder_1_out2, decoder_2_out7);
endmodule

module x6 (
  input  [3:0] in_1,
  input  [3:0] in_2,
  output out_3
);

  wire decoder_1_out3, decoder_2_out5;

  Decoder #(.select(4)) decoder_1 (
    .out3(decoder_1_out3), .sel(in_1));  // open: out0, out1, out2, out4, out5, out6, out7, out8, out9, out10, out11, out12, out13, out14, out15, en
  Decoder #(.select(4)) decoder_2 (
    .out5(decoder_2_out5), .sel(in_2));  // open: out0, out1, out2, out3, out4, out6, out7, out8, out9, out10, out11, out12, out13, out14, out15, en
  and q2t5 (out_3, decoder_1_out3, decoder_2_out5);
endmodule

module x10 (
  input  [3:0] in_1,
  input  [3:0] in_2,
  output out_3
);

  wire decoder_1_out4, decoder_2_out8;

  Decoder #(.select(4)) decoder_1 (
    .out4(decoder_1_out4), .sel(in_1));  // open: out0, out1, out2, out3, out5, out6, out7, out8, out9, out10, out11, out12, out13, out14, out15, en
  Decoder #(.select(4)) decoder_2 (
    .out8(decoder_2_out8), .sel(in_2));  // open: out0, out1, out2, out3, out4, out5, out6, out7, out9, out10, out11, out12, out13, out14, out15, en
  and q3t8 (out_3, decoder_1_out4, decoder_2_out8);
endmodule

module x11 (
  input  [3:0] in_1,
  input  [3:0] in_2,
  output out_3
);

  wire decoder_1_out4, decoder_2_out8;

  Decoder #(.select(4)) decoder_1 (
    .out4(decoder_1_out4), .sel(in_1));  // open: out0, out1, out2, out3, out5, out6, out7, out8, out9, out10, out11, out12, out13, out14, out15, en
  Decoder #(.select(4)) decoder_2 (
    .out8(decoder_2_out8), .sel(in_2));  // open: out0, out1, out2, out3, out4, out5, out6, out7, out9, out10, out11, out12, out13, out14, out15, en
  and q3t8 (out_3, decoder_1_out4, decoder_2_out8);
endmodule

module x4 (
  input  [3:0] in_1,
  output out_2
);

  Decoder #(.select(4)) decoder_1 (
    .out2(out_2), .sel(in_1));  // open: out0, out1, out3, out4, out5, out6, out7, out8, out9, out10, out11, out12, out13, out14, out15, en
endmodule

module UC (
  input  [3:0] in_1,
  input  [3:0] in_2,
  output out_3,
  output out_4,
  output out_5,
  output out_6,
  output out_7,
  output out_8,
  output out_9,
  output out_10,
  output out_11,
  output out_12,
  output out_13,
  output out_14
);

  x0 x_0 (.q(in_1), .t(in_2), .out_3(out_3));
  x1 x1 (.q(in_1), .t(in_2), .out_3(out_4));
  x2 x2 (.q(in_1), .t(in_2), .out_3(out_5));
  x3 x3 (.q(in_1), .t(in_2), .out_3(out_6));
  x4 x4 (.in_1(in_2), .out_2(out_7));
  x5 x5 (.q(in_1), .t(in_2), .out_3(out_8));
  x6 x6 (.in_1(in_1), .in_2(in_2), .out_3(out_9));
  x7 x7 (.q(in_1), .t(in_2), .out_3(out_10));
  x8 x_8 (.q(in_1), .t(in_2), .out_3(out_11));
  x9 x_9 (.in_1(in_1), .in_2(in_2), .out_3(out_12));
  x10 x_10 (.in_1(in_1), .in_2(in_2), .out_3(out_13));
  x11 x11 (.in_1(in_1), .in_2(in_2), .out_3(out_14));
endmodule
