// Logisim project problema1.circ as structural Verilog: 1 circuit, main circuit main
module main (
  input  A,
  input  B,
  input  C,
  input  D,
  output out_5
);

  wire and_1_out, and_2_out, not_1_out, not_2_out, not_3_out, not_4_out, not_5_out;

  not not_1 (not_1_out, C);
  not not_2 (not_2_out, A);
  not not_3 (not_3_out, D);
  not not_4 (not_4_out, C);
  not not_5 (not_5_out, D);
  and and_1 (and_1_out, A, not_1_out, not_3_out);
  and and_2 (and_2_out, not_2_out, B, not_4_out, not_5_out);
  or or_1 (out_5, and_1_out, and_2_out);
endmodule
