// Logisim project problema2.circ as structural Verilog: 1 circuit, main circuit main
module main (
  input  A,
  input  B,
  input  C_in,
  output A_B,
  output C_out
);

  wire and_1_out, and_2_out, and_3_out, or_1_out, xor_1_out;

  and and_1 (and_1_out, C_in, A);
  and and_2 (and_2_out, C_in, B);
  xor xor_1 (xor_1_out, A, B);
  and and_3 (and_3_out, A, B);
  or or_1 (or_1_out, and_3_out, and_1_out);
  xor xor_2 (A_B, xor_1_out, C_in);
  or or_2 (C_out, or_1_out, and_2_out);
endmodule
