// Logisim project problema3.circ as structural Verilog: 1 circuit, main circuit main
module main (
  input  A,
  input  A_2,
  input  B,
  input  B_2,
  input  C_in,
  input  A_3,
  input  B_3,
  input  A_4,
  input  A_5,
  input  B_4,
  input  B_5,
  output A_B,
  output A_B_2,
  output A_B_3,
  output A_B_4,
  output A_B_5,
  output C_out
);

  wire and_1_out, and_2_out, and_3_out, and_4_out, and_5_out, and_6_out, and_7_out, and_8_out, and_9_out,
       and_10_out, and_11_out, and_12_out, and_13_out, and_14_out, and_15_out, or_1_out, or_2_out, or_3_out,
       or_4_out, or_5_out, or_6_out, or_7_out, or_8_out, or_9_out, xor_1_out, xor_2_out, xor_5_out,
       xor_6_out, xor_9_out;

  and and_1 (and_1_out, C_in, A);
  and and_2 (and_2_out, C_in, B);
  and and_3 (and_3_out, or_3_out, A_5);
  and and_4 (and_4_out, or_3_out, B_5);
  xor xor_1 (xor_1_out, A, B);
  and and_5 (and_5_out, A, B);
  or or_1 (or_1_out, and_5_out, and_1_out);
  xor xor_2 (xor_2_out, A_5, B_5);
  and and_6 (and_6_out, A_5, B_5);
  or or_2 (or_2_out, and_6_out, and_3_out);
  xor xor_3 (A_B, xor_1_out, C_in);
  or or_3 (or_3_out, or_1_out, and_2_out);
  xor xor_4 (A_B_5, xor_2_out, or_3_out);
  or or_4 (or_4_out, or_2_out, and_4_out);
  and and_7 (and_7_out, or_4_out, A_2);
  and and_8 (and_8_out, or_4_out, B_2);
  xor xor_5 (xor_5_out, A_2, B_2);
  and and_9 (and_9_out, A_2, B_2);
  or or_5 (or_5_out, and_9_out, and_7_out);
  xor xor_6 (xor_6_out, A_4, B_4);
  and and_10 (and_10_out, A_4, B_4);
  and and_11 (and_11_out, or_6_out, A_4);
  and and_12 (and_12_out, or_6_out, B_4);
  xor xor_7 (A_B_2, xor_5_out, or_4_out);
  or or_6 (or_6_out, or_5_out, and_8_out);
  xor xor_8 (A_B_4, xor_6_out, or_6_out);
  or or_7 (or_7_out, and_10_out, and_11_out);
  or or_8 (or_8_out, or_7_out, and_12_out);
  and and_13 (and_13_out, or_8_out, A_3);
  and and_14 (and_14_out, or_8_out, B_3);
  xor xor_9 (xor_9_out, A_3, B_3);
  and and_15 (and_15_out, A_3, B_3);
  or or_9 (or_9_out, and_15_out, and_13_out);
  xor xor_10 (A_B_3, xor_9_out, or_8_out);
  or or_10 (C_out, or_9_out, and_14_out);

  // Notes on the sheet:
  //   C_in
  //   C_out
  //   C_out
  //   C_in
  //   C_in
  //   C_out
  //   C_out
  //   C_in
endmodule
